// Logisim project main.circ as structural Verilog: 1 circuit, main circuit main
module main (
  output [39:0] out_1,
  output [7:0] out_2,
  output [3:0] out_3,
  output [3:0] out_4,
  output [15:0] out_5,
  output [15:0] out_6,
  output [8:0] out_7
);

  wire CLK, N_CLK, RESET;
  wire [2:0] ARG1_CHOICE, ARG2_CHOICE;
  wire [15:0] ARG1_ENTRY_VALUE, ARG2_ENTRY_VALUE, R0_q, R2_q, R3_q, R4_q, R5_q, R6_q, R7_q;

  Clock clock_1 (.out(CLK));
  Button button_1 (.out(RESET));
  Counter #(.max('h1ff), .width(9)) counter_1 (.clr(RESET), .clk(CLK), .Q(out_7));  // open: load, up, count, D, carry
  ROM #(.addrWidth(9), .dataWidth(40)) PROG (.addr(out_7), .data(out_1));
  Register #(.width(16)) R0 (.clk(N_CLK), .Q(R0_q), .clr(RESET));  // open: D, en
  Register #(.width(16)) R1 (.clk(N_CLK), .Q(R0_q), .clr(RESET));  // open: D, en
  Register #(.width(16)) R2 (.clk(N_CLK), .Q(R2_q), .clr(RESET));  // open: D, en
  Register #(.width(16)) R3 (.clk(N_CLK), .Q(R3_q), .clr(RESET));  // open: D, en
  Register #(.width(16)) R4 (.clk(N_CLK), .Q(R4_q), .clr(RESET));  // open: D, en
  Register #(.width(16)) R5 (.clk(N_CLK), .Q(R5_q), .clr(RESET));  // open: D, en
  Register #(.width(16)) R6 (.clk(N_CLK), .Q(R6_q), .clr(RESET));  // open: D, en
  Register #(.width(16)) R7 (.clk(N_CLK), .Q(R7_q), .clr(RESET));  // open: D, en
  RAM #(.addrWidth(16), .dataWidth(16)) MEMORY ();  // open: addr, we, oe, clk, din, dout
  Multiplexer #(.select(3), .width(16)) multiplexer_1 (
    .in0(R0_q), .in1(R0_q), .in2(R2_q), .in3(R3_q), .in4(R4_q), .in5(R5_q), .in6(R6_q), .in7(R7_q),
    .out(ARG1_ENTRY_VALUE), .sel(ARG1_CHOICE));
  Multiplexer #(.select(3), .width(16)) multiplexer_2 (
    .in0(R0_q), .in1(R0_q), .in2(R2_q), .in3(R3_q), .in4(R4_q), .in5(R5_q), .in6(R6_q), .in7(R7_q),
    .out(ARG2_ENTRY_VALUE), .sel(ARG2_CHOICE));

  assign out_2 = out_1[39:32];
  assign out_3 = out_1[39:36];
  assign out_4 = out_1[35:32];
  assign out_5 = out_1[31:16];
  assign out_6 = out_1[15:0];

  // Other names for the same wires on the sheet: INT_ARG2[15:0] = out_1[15:0]; INT_BITFIELD[39:0] = out_1;
  //   INT_ARG1[15:0] = out_1[31:16]; INT_OP_TYPE2[3:0] = out_1[35:32]; INT_OPCODE[7:0] = out_1[39:32];
  //   INT_OP_TYPE1[3:0] = out_1[39:36]; INT_COUNTER[8:0] = out_7

  // Notes on the sheet:
  //   contents of PROG (hex, n*v repeats v):
  //   200320000 200000001 200010002 1100020000 1000020001 2100020000 3000030000 100010020 200410050
endmodule
